// Logisim project additionneur_8_bit_et_additionneur_soustracteur_8_bit_Lou_Eouzan.circ as structural Verilog: 4 circuits, main circuit additionneur_8_bit
module additionneur_8_bit (
  input  in_1,
  input  in_2,
  input  in_3,
  input  in_4,
  input  in_5,
  input  in_6,
  input  in_7,
  input  in_8,
  input  in_9,
  input  in_10,
  input  in_11,
  input  in_12,
  input  in_13,
  input  in_14,
  input  in_15,
  input  in_16,
  output out_17,
  output out_18,
  output out_19,
  output out_20,
  output out_21,
  output out_22,
  output out_23,
  output out_24,
  output out_25
);

  wire additionneur_1_carry, additionneur_2_carry, additionneur_3_carry, additionneur_4_carry,
       additionneur_5_carry, additionneur_6_carry, additionneur_7_carry;

  additionneur additionneur_1 (.in_1(in_8), .in_2(in_16), .in_3(1'b0), .carry(additionneur_1_carry), .sum(out_25));
  additionneur additionneur_2 (
    .in_1(in_7), .in_2(in_15), .in_3(additionneur_1_carry), .carry(additionneur_2_carry), .sum(out_24));
  additionneur additionneur_3 (
    .in_1(in_6), .in_2(in_14), .in_3(additionneur_2_carry), .carry(additionneur_3_carry), .sum(out_23));
  additionneur additionneur_4 (
    .in_1(in_5), .in_2(in_13), .in_3(additionneur_3_carry), .carry(additionneur_4_carry), .sum(out_22));
  additionneur additionneur_5 (
    .in_1(in_4), .in_2(in_12), .in_3(additionneur_4_carry), .carry(additionneur_5_carry), .sum(out_21));
  additionneur additionneur_6 (
    .in_1(in_3), .in_2(in_11), .in_3(additionneur_5_carry), .carry(additionneur_6_carry), .sum(out_20));
  additionneur additionneur_7 (
    .in_1(in_2), .in_2(in_10), .in_3(additionneur_6_carry), .carry(additionneur_7_carry), .sum(out_19));
  additionneur additionneur_8 (.in_1(in_1), .in_2(in_9), .in_3(additionneur_7_carry), .carry(out_17), .sum(out_18));
endmodule

module additionneur_soustracteur_8_bit (
  input  in_1,
  input  in_2,
  input  in_3,
  input  in_4,
  input  in_5,
  input  in_6,
  input  in_7,
  input  in_8,
  input  in_9,
  input  in_10,
  input  in_11,
  input  in_12,
  input  in_13,
  input  in_14,
  input  in_15,
  input  in_16,
  output out_17,
  output out_18,
  output out_19,
  output out_20,
  output out_21,
  output out_22,
  output out_23,
  output out_24,
  output out_25
);

  wire additionneur_1_carry, additionneur_2_carry, additionneur_3_carry, additionneur_4_carry,
       additionneur_5_carry, additionneur_6_carry, additionneur_7_carry, not_1_out, not_2_out, not_3_out,
       not_4_out, not_5_out, not_6_out, not_7_out, not_8_out, or_1_out, or_2_out, or_3_out, or_4_out,
       or_5_out, or_6_out, or_7_out, or_8_out;

  not not_1 (not_1_out, in_9);
  not not_2 (not_2_out, in_10);
  not not_3 (not_3_out, in_11);
  not not_4 (not_4_out, in_12);
  not not_5 (not_5_out, in_13);
  not not_6 (not_6_out, in_14);
  not not_7 (not_7_out, in_15);
  not not_8 (not_8_out, in_16);
  or or_1 (or_1_out, not_1_out, 1'b1);
  or or_2 (or_2_out, not_2_out, 1'b1);
  or or_3 (or_3_out, not_3_out, 1'b1);
  or or_4 (or_4_out, not_4_out, 1'b1);
  or or_5 (or_5_out, not_5_out, 1'b1);
  or or_6 (or_6_out, not_6_out, 1'b1);
  or or_7 (or_7_out, not_7_out, 1'b1);
  or or_8 (or_8_out, not_8_out, 1'b1);
  additionneur additionneur_1 (.in_1(in_8), .in_2(or_8_out), .in_3(1'b0), .carry(additionneur_1_carry), .sum(out_25));
  additionneur additionneur_2 (
    .in_1(in_7), .in_2(or_7_out), .in_3(additionneur_1_carry), .carry(additionneur_2_carry), .sum(out_24));
  additionneur additionneur_3 (
    .in_1(in_6), .in_2(or_6_out), .in_3(additionneur_2_carry), .carry(additionneur_3_carry), .sum(out_23));
  additionneur additionneur_4 (
    .in_1(in_5), .in_2(or_5_out), .in_3(additionneur_3_carry), .carry(additionneur_4_carry), .sum(out_22));
  additionneur additionneur_5 (
    .in_1(in_4), .in_2(or_4_out), .in_3(additionneur_4_carry), .carry(additionneur_5_carry), .sum(out_21));
  additionneur additionneur_6 (
    .in_1(in_3), .in_2(or_3_out), .in_3(additionneur_5_carry), .carry(additionneur_6_carry), .sum(out_20));
  additionneur additionneur_7 (
    .in_1(in_2), .in_2(or_2_out), .in_3(additionneur_6_carry), .carry(additionneur_7_carry), .sum(out_19));
  additionneur additionneur_8 (.in_1(in_1), .in_2(or_1_out), .in_3(additionneur_7_carry), .carry(out_17), .sum(out_18));
endmodule

module demi_additionneur (
  input  in_1,
  input  in_2,
  output carry,
  output sum
);

  wire not_1_out, or_1_out;

  and and_1 (carry, in_1, in_2);
  or or_1 (or_1_out, in_1, in_2);
  not not_1 (not_1_out, carry);
  and and_2 (sum, not_1_out, or_1_out);
endmodule

module additionneur (
  input  in_1,
  input  in_2,
  input  in_3,
  output carry,
  output sum
);

  wire demi_additionneur_1_carry, demi_additionneur_1_sum, demi_additionneur_2_carry;

  demi_additionneur demi_additionneur_1 (
    .in_1(in_1), .in_2(in_2), .carry(demi_additionneur_1_carry), .sum(demi_additionneur_1_sum));
  demi_additionneur demi_additionneur_2 (
    .in_1(demi_additionneur_1_sum), .in_2(in_3), .carry(demi_additionneur_2_carry), .sum(sum));
  or or_1 (carry, demi_additionneur_1_carry, demi_additionneur_2_carry);
endmodule
